// Logisim project simulacion.circ as structural Verilog
module Control (
  input  S,
  input  L,
  input  V,
  input  F,
  output Out
);

  wire and_1_out, and_2_out, not_1_out, not_2_out;

  not not_1 (not_1_out, S);
  and and_1 (and_1_out, not_1_out, V);
  and and_2 (and_2_out, S, not_2_out);
  not not_2 (not_2_out, F);
  or or_1 (Out, and_1_out, L, and_2_out);
endmodule

module FinalControl (
  input  S,
  input  L,
  input  V,
  input  F,
  output Out
);

  wire and_1_out, and_2_out, and_3_out, and_4_out, not_1_out, not_2_out, not_3_out, not_4_out;

  not not_1 (not_1_out, S);
  and and_1 (and_1_out, not_1_out, not_2_out);
  not not_2 (not_2_out, L);
  and and_2 (and_2_out, S, not_3_out);
  not not_3 (not_3_out, L);
  not not_4 (not_4_out, F);
  and and_3 (and_3_out, and_1_out, V);
  and and_4 (and_4_out, and_2_out, not_4_out);
  or or_1 (Out, and_3_out, and_4_out);
endmodule
